# Fritzing sketch Wall-e (saved by Fritzing 0.9.3b)

parts:
  S1 = H-Bridge with L298N
  M1 = DC Motor
  M2 = DC Motor
  Componente1 = Arduino Nano (Rev3.0) (ICSP)
  HC-SR04_Sensor_1 = HC-SR04 Ultrasonic Distance Sensor
  Componente2 = Bluetooth HC-05 Macho
  VCC1 = Battery block 9V
  LED2 = LED - 5mm [color="Red (633nm)" package="5 mm [THT]"]
  LED3 = LED - 5mm [color="Red (633nm)" package="5 mm [THT]"]  # not connected
  LED1 = LED - 5mm [color="Red (633nm)" package="5 mm [THT]"]
  R3 = Resistor [tolerance=±5% resistance=220 package="0805 [SMD]"]  # not connected
  R4 = Resistor [tolerance=±5% resistance=220 package=THT]
  R5 = Resistor [tolerance=±5% resistance=220 package=THT]
  R6 = Resistor [tolerance=±5% resistance=220 package=THT]

nets:
  N1: S1.12V, VCC1.+
  N2: S1.GND, VCC1.-
  N3: S1.IN1, Componente1.D7
  N4: S1.IN2, Componente1.D6
  N5: S1.IN3, Componente1.D4
  N6: S1.IN4, Componente1.D2
  N7: S1.OUT3-Motor2, M1.pin_2
  N8: S1.OUT4-Motor2, M1.pin_1
  N9: S1.OUT1-Motor1, M2.pin_1
  N10: S1.OUT2-Motor1, M2.pin_2
  N11: Componente1.D0/RX, Componente2.TXD
  N12: Componente1.GND, LED2.anode, LED1.anode
  N13: Componente1.D8, HC-SR04_Sensor_1.TRIG
  N14: Componente1.D9, HC-SR04_Sensor_1.ECHO
  N15: Componente1.D10, R4.Pin_0
  N16: Componente1.D11/MOSI, R5.Pin_0
  N17: Componente1.D12/MISO, R6.Pin_0
  VCC: Componente1.5V, HC-SR04_Sensor_1.VCC, Componente2.VCC
  GND: HC-SR04_Sensor_1.GND, Componente2.GND

custom parts:
  H-Bridge with L298N: h-bridge
